// Logisim project MIPS32SingleCycle.circ as structural Verilog: 12 circuits, main circuit main
module main (
  input  ClearPC,
  input  ClearCPU,
  output [15:0] Immediate_16,
  output [31:0] out_4,
  output [31:0] OperandA,
  output [31:0] OperandB,
  output [31:0] ALUResult,
  output [5:0] out_8,
  output [5:0] out_9,
  output [31:0] out_10,
  output [31:0] ProgramCounter,
  output [4:0] Register_1,
  output [4:0] Register_2,
  output [4:0] Write_Register
);

  wire alucontrol_1_ainv, alucontrol_1_binv, ALUSrc, ALUZero, Branch, CLK, Jump, MRead, MToReg, MWrite,
       or_1_out, OverF, RDst, RegWrite;
  wire [1:0] alucontrol_1_aluoperationsel, ALUOp;
  wire [4:0] instregister_1_writereg;
  wire [25:0] JumpA;
  wire [31:0] datainstmemory_2_memdata, NewPC, registerbank_1_register2, SExtImmd;

  Register #(.width(32)) PC (.D(NewPC), .en(1'b1), .clk(CLK), .Q(ProgramCounter), .clr(or_1_out));
  or or_1 (or_1_out, ClearPC, ClearCPU);
  NewPCCircuit newpccircuit_1 (
    .Branch(Branch), .Jump(Jump), .ALUZero(ALUZero), .PC(ProgramCounter), .SExtImmd(SExtImmd), .JAddr(JumpA),
    .out_7(NewPC));
  DataInstMemory datainstmemory_1 (
    .Address(ProgramCounter), .MemWrite(1'b0), .MemRead(1'b1), .CLK(CLK), .MemData(out_4));  // open: Write_Data
  InstRegister instregister_1 (
    .Instruction(out_4), .OpCode(out_8), .ReadReg1(Register_1), .ReadReg2(Register_2),
    .WriteReg(instregister_1_writereg), .Funct(out_9), .Immd16(Immediate_16), .Jump(JumpA));
  Multiplexer #(.width(5)) multiplexer_1 (
    .in0(Register_2), .in1(instregister_1_writereg), .out(Write_Register), .sel(RDst));
  assign SExtImmd = {{16{Immediate_16[15]}}, Immediate_16};  // Bit_Extender bit_extender_1
  ControlUnit controlunit_1 (
    .Opcode(out_8), .ALUSrc(ALUSrc), .MemToReg(MToReg), .RegWrite(RegWrite), .MemRead(MRead),
    .MemWrite(MWrite), .Branch(Branch), .Jump(Jump), .ALUOp(ALUOp), .RegDst(RDst));
  Clock clock_1 (.out(CLK));
  RegisterBank registerbank_1 (
    .ReadRegister2(Register_2), .WriteRegister(Write_Register), .WriteData(out_10), .Clock(CLK),
    .ClearPin(ClearCPU), .RegWrite(RegWrite), .ReadRegister1(Register_1),
    .Register2(registerbank_1_register2), .Register1(OperandA));
  Multiplexer #(.width(32)) multiplexer_2 (
    .in0(registerbank_1_register2), .in1(SExtImmd), .out(OperandB), .sel(ALUSrc));
  ALUControl alucontrol_1 (
    .Funct(out_9), .ALUOp(ALUOp), .AInv(alucontrol_1_ainv), .BInv(alucontrol_1_binv),
    .ALUOperationSel(alucontrol_1_aluoperationsel));
  ALU32Bits alu32bits_1 (
    .OperandA(OperandA), .OperandB(OperandB), .AInv(alucontrol_1_ainv), .BInv(alucontrol_1_binv),
    .ALUOp(alucontrol_1_aluoperationsel), .ALUResult(ALUResult), .Overflow(OverF), .ZeroComp(ALUZero));
  LED led_1 (.in(OverF));
  DataInstMemory datainstmemory_2 (
    .Address(ALUResult), .MemWrite(MWrite), .MemRead(MRead), .CLK(CLK),
    .Write_Data(registerbank_1_register2), .MemData(datainstmemory_2_memdata));
  Multiplexer #(.width(32)) multiplexer_3 (.in0(ALUResult), .in1(datainstmemory_2_memdata), .out(out_10), .sel(MToReg));

  // Other names for the same wires on the sheet: ARes[31:0] = ALUResult; Funct[5:0] = out_9;
  //   Immd16[15:0] = Immediate_16; Inst[31:0] = out_4; OPa[31:0] = OperandA; OPb[31:0] = OperandB;
  //   Opcode[5:0] = out_8; PC[31:0] = ProgramCounter; Reg1[4:0] = Register_1; Reg2[4:0] = Register_2;
  //   WData[31:0] = out_10; WReg[4:0] = Write_Register

  // Notes on the sheet:
  //   INST
  //   Instruction
  //   ALUOverflow
  //   DATA
endmodule

module DataInstMemory (
  input  [31:0] Address,
  input  MemWrite,
  input  MemRead,
  input  [31:0] Write_Data,
  input  CLK,
  output [31:0] MemData
);

  wire [31:0] shifter_1_out;

  Shifter #(.shift("lr"), .width(32)) shifter_1 (.in(Address), .\dist (5'b00010), .out(shifter_1_out));
  RAM #(.addrWidth(16), .asyncread("true"), .dataWidth(32)) ram_1 (
    .addr(shifter_1_out[15:0]), .we(MemWrite), .oe(MemRead), .clk(CLK), .din(Write_Data), .dout(MemData));
endmodule

module InstRegister (
  input  [31:0] Instruction,
  output [5:0] OpCode,
  output [4:0] ReadReg1,
  output [4:0] ReadReg2,
  output [4:0] WriteReg,
  output [5:0] Funct,
  output [15:0] Immd16,
  output [25:0] Jump
);


  assign Funct = Instruction[5:0];
  assign Immd16 = Instruction[15:0];
  assign Jump = Instruction[25:0];
  assign OpCode = Instruction[31:26];
  assign ReadReg1 = Instruction[25:21];
  assign ReadReg2 = Instruction[20:16];
  assign WriteReg = Instruction[15:11];
endmodule

module ControlUnit (
  input  [5:0] Opcode,
  output RegDst,
  output ALUSrc,
  output MemToReg,
  output RegWrite,
  output MemRead,
  output MemWrite,
  output Branch,
  output Jump,
  output [1:0] ALUOp
);

  wire and_2_out, and_3_out, and_4_out, and_5_out, and_6_out, and_9_out, and_10_out, and_11_out, and_12_out,
       and_13_out, and_14_out, and_15_out, and_17_out, and_18_out, and_19_out, and_20_out, not_1_out,
       not_2_out, not_3_out, not_4_out, not_5_out, not_6_out;

  not not_1 (not_1_out, Opcode[5]);
  not not_2 (not_2_out, Opcode[4]);
  not not_3 (not_3_out, Opcode[3]);
  not not_4 (not_4_out, Opcode[2]);
  not not_5 (not_5_out, Opcode[1]);
  not not_6 (not_6_out, Opcode[0]);
  and and_1 (RegDst, not_1_out, not_2_out, not_3_out, not_4_out, not_5_out, not_6_out);
  and and_2 (and_2_out, Opcode[3], not_4_out, not_5_out);
  and and_3 (and_3_out, Opcode[4], not_4_out, not_5_out);
  and and_4 (and_4_out, Opcode[5], not_4_out, not_5_out);
  and and_5 (and_5_out, not_3_out, Opcode[0]);
  and and_6 (and_6_out, not_4_out, not_5_out);
  and and_7 (MemRead, not_3_out, Opcode[0]);
  and and_8 (MemWrite, Opcode[3], Opcode[1]);
  and and_9 (and_9_out, Opcode[5], not_3_out, not_5_out);
  and and_10 (and_10_out, not_3_out, not_5_out, Opcode[0]);
  and and_11 (and_11_out, not_3_out, Opcode[2], not_5_out);
  and and_12 (and_12_out, Opcode[4], not_3_out, not_5_out);
  and and_13 (and_13_out, Opcode[4], not_3_out, not_4_out, not_6_out);
  and and_14 (and_14_out, Opcode[5], not_3_out, not_4_out, not_6_out);
  and and_15 (and_15_out, not_3_out, not_4_out, Opcode[1], not_6_out);
  and and_16 (ALUOp[1], not_1_out, not_2_out, not_3_out, not_4_out, not_5_out, not_6_out);
  and and_17 (and_17_out, Opcode[5], not_3_out, not_5_out);
  and and_18 (and_18_out, not_3_out, not_5_out, Opcode[0]);
  and and_19 (and_19_out, not_3_out, Opcode[2], not_5_out);
  and and_20 (and_20_out, Opcode[4], not_3_out, not_5_out);
  or or_1 (ALUSrc, Opcode[0], and_2_out, and_3_out, and_4_out);
  or or_2 (RegWrite, and_5_out, and_6_out);
  or or_3 (Branch, and_9_out, and_10_out, and_11_out, and_12_out);
  or or_4 (Jump, and_13_out, and_14_out, and_15_out);
  or or_5 (ALUOp[0], and_17_out, and_18_out, and_19_out, and_20_out);

  assign MemToReg = Opcode[0];
endmodule

module RegisterBank (
  input  RegWrite,
  input  [4:0] WriteRegister,
  input  [31:0] WriteData,
  input  Clock,
  input  ClearPin,
  input  [4:0] ReadRegister1,
  input  [4:0] ReadRegister2,
  output [31:0] Register1,
  output [31:0] Register2
);

  wire [6:0] decoder_1_out1;
  wire [7:0] decoder_1_out8, decoder_1_out16, decoder_1_out24;
  wire [31:0] genericreg_1_probe, genericreg_1_regout, genericreg_2_probe, genericreg_2_regout,
       genericreg_3_probe, genericreg_3_regout, genericreg_4_probe, genericreg_4_regout, genericreg_5_probe,
       genericreg_5_regout, genericreg_6_probe, genericreg_6_regout, genericreg_7_probe, genericreg_7_regout,
       genericreg_8_probe, genericreg_8_regout, genericreg_9_probe, genericreg_9_regout, genericreg_10_probe,
       genericreg_10_regout, genericreg_11_probe, genericreg_11_regout, genericreg_12_probe,
       genericreg_12_regout, genericreg_13_probe, genericreg_13_regout, genericreg_14_probe,
       genericreg_14_regout, genericreg_15_probe, genericreg_15_regout, genericreg_16_probe,
       genericreg_16_regout, genericreg_17_probe, genericreg_17_regout, genericreg_18_probe,
       genericreg_18_regout, genericreg_19_probe, genericreg_19_regout, genericreg_20_probe,
       genericreg_20_regout, genericreg_21_probe, genericreg_21_regout, genericreg_22_probe,
       genericreg_22_regout, genericreg_23_probe, genericreg_23_regout, genericreg_24_probe,
       genericreg_24_regout, genericreg_25_probe, genericreg_25_regout, genericreg_26_probe,
       genericreg_26_regout, genericreg_27_probe, genericreg_27_regout, genericreg_28_probe,
       genericreg_28_regout, genericreg_29_probe, genericreg_29_regout, genericreg_30_probe,
       genericreg_30_regout, genericreg_31_probe, genericreg_31_regout, genericreg_32_probe,
       genericreg_32_regout;

  Decoder #(.select(5)) decoder_1 (
    .out1(decoder_1_out1[0]), .out2(decoder_1_out1[1]), .out3(decoder_1_out1[2]), .out4(decoder_1_out1[3]),
    .out5(decoder_1_out1[4]), .out6(decoder_1_out1[5]), .out7(decoder_1_out1[6]), .out8(decoder_1_out8[0]),
    .out9(decoder_1_out8[1]), .out10(decoder_1_out8[2]), .out11(decoder_1_out8[3]),
    .out12(decoder_1_out8[4]), .out13(decoder_1_out8[5]), .out14(decoder_1_out8[6]),
    .out15(decoder_1_out8[7]), .out16(decoder_1_out16[0]), .out17(decoder_1_out16[1]),
    .out18(decoder_1_out16[2]), .out19(decoder_1_out16[3]), .out20(decoder_1_out16[4]),
    .out21(decoder_1_out16[5]), .out22(decoder_1_out16[6]), .out23(decoder_1_out16[7]),
    .out24(decoder_1_out24[0]), .out25(decoder_1_out24[1]), .out26(decoder_1_out24[2]),
    .out27(decoder_1_out24[3]), .out28(decoder_1_out24[4]), .out29(decoder_1_out24[5]),
    .out30(decoder_1_out24[6]), .out31(decoder_1_out24[7]), .sel(WriteRegister), .en(RegWrite));  // open: out0
  // Probe on genericreg_1_probe
  // Probe on genericreg_2_probe
  // Probe on genericreg_3_probe
  // Probe on genericreg_4_probe
  // Probe on genericreg_5_probe
  // Probe on genericreg_6_probe
  // Probe on genericreg_7_probe
  // Probe on genericreg_8_probe
  Multiplexer #(.select(5), .width(32)) multiplexer_1 (
    .in0(genericreg_1_regout), .in1(genericreg_2_regout), .in2(genericreg_3_regout),
    .in3(genericreg_4_regout), .in4(genericreg_5_regout), .in5(genericreg_6_regout),
    .in6(genericreg_7_regout), .in7(genericreg_8_regout), .in8(genericreg_9_regout),
    .in9(genericreg_10_regout), .in10(genericreg_11_regout), .in11(genericreg_12_regout),
    .in12(genericreg_13_regout), .in13(genericreg_14_regout), .in14(genericreg_15_regout),
    .in15(genericreg_16_regout), .in16(genericreg_17_regout), .in17(genericreg_18_regout),
    .in18(genericreg_19_regout), .in19(genericreg_20_regout), .in20(genericreg_21_regout),
    .in21(genericreg_22_regout), .in22(genericreg_23_regout), .in23(genericreg_24_regout),
    .in24(genericreg_25_regout), .in25(genericreg_26_regout), .in26(genericreg_27_regout),
    .in27(genericreg_28_regout), .in28(genericreg_29_regout), .in29(genericreg_30_regout),
    .in30(genericreg_31_regout), .in31(genericreg_32_regout), .out(Register1), .sel(ReadRegister1));
  GenericReg genericreg_1 (
    .WriteEnable(1'b0), .CLK(Clock), .ClearPin(ClearPin), .Probe(genericreg_1_probe),
    .RegOut(genericreg_1_regout));  // open: WriteData
  GenericReg genericreg_2 (
    .WriteData(WriteData), .WriteEnable(decoder_1_out1[0]), .CLK(Clock), .ClearPin(ClearPin),
    .Probe(genericreg_2_probe), .RegOut(genericreg_2_regout));
  GenericReg genericreg_3 (
    .WriteData(WriteData), .WriteEnable(decoder_1_out1[1]), .CLK(Clock), .ClearPin(ClearPin),
    .Probe(genericreg_3_probe), .RegOut(genericreg_3_regout));
  GenericReg genericreg_4 (
    .WriteData(WriteData), .WriteEnable(decoder_1_out1[2]), .CLK(Clock), .ClearPin(ClearPin),
    .Probe(genericreg_4_probe), .RegOut(genericreg_4_regout));
  GenericReg genericreg_5 (
    .WriteData(WriteData), .WriteEnable(decoder_1_out1[3]), .CLK(Clock), .ClearPin(ClearPin),
    .Probe(genericreg_5_probe), .RegOut(genericreg_5_regout));
  GenericReg genericreg_6 (
    .WriteData(WriteData), .WriteEnable(decoder_1_out1[4]), .CLK(Clock), .ClearPin(ClearPin),
    .Probe(genericreg_6_probe), .RegOut(genericreg_6_regout));
  GenericReg genericreg_7 (
    .WriteData(WriteData), .WriteEnable(decoder_1_out1[5]), .CLK(Clock), .ClearPin(ClearPin),
    .Probe(genericreg_7_probe), .RegOut(genericreg_7_regout));
  GenericReg genericreg_8 (
    .WriteData(WriteData), .WriteEnable(decoder_1_out1[6]), .CLK(Clock), .ClearPin(ClearPin),
    .Probe(genericreg_8_probe), .RegOut(genericreg_8_regout));
  // Probe on genericreg_9_probe
  GenericReg genericreg_9 (
    .WriteData(WriteData), .WriteEnable(decoder_1_out8[0]), .CLK(Clock), .ClearPin(ClearPin),
    .Probe(genericreg_9_probe), .RegOut(genericreg_9_regout));
  // Probe on genericreg_10_probe
  GenericReg genericreg_10 (
    .WriteData(WriteData), .WriteEnable(decoder_1_out8[1]), .CLK(Clock), .ClearPin(ClearPin),
    .Probe(genericreg_10_probe), .RegOut(genericreg_10_regout));
  // Probe on genericreg_11_probe
  GenericReg genericreg_11 (
    .WriteData(WriteData), .WriteEnable(decoder_1_out8[2]), .CLK(Clock), .ClearPin(ClearPin),
    .Probe(genericreg_11_probe), .RegOut(genericreg_11_regout));
  // Probe on genericreg_12_probe
  GenericReg genericreg_12 (
    .WriteData(WriteData), .WriteEnable(decoder_1_out8[3]), .CLK(Clock), .ClearPin(ClearPin),
    .Probe(genericreg_12_probe), .RegOut(genericreg_12_regout));
  // Probe on genericreg_13_probe
  GenericReg genericreg_13 (
    .WriteData(WriteData), .WriteEnable(decoder_1_out8[4]), .CLK(Clock), .ClearPin(ClearPin),
    .Probe(genericreg_13_probe), .RegOut(genericreg_13_regout));
  // Probe on genericreg_14_probe
  GenericReg genericreg_14 (
    .WriteData(WriteData), .WriteEnable(decoder_1_out8[5]), .CLK(Clock), .ClearPin(ClearPin),
    .Probe(genericreg_14_probe), .RegOut(genericreg_14_regout));
  // Probe on genericreg_15_probe
  GenericReg genericreg_15 (
    .WriteData(WriteData), .WriteEnable(decoder_1_out8[6]), .CLK(Clock), .ClearPin(ClearPin),
    .Probe(genericreg_15_probe), .RegOut(genericreg_15_regout));
  // Probe on genericreg_16_probe
  GenericReg genericreg_16 (
    .WriteData(WriteData), .WriteEnable(decoder_1_out8[7]), .CLK(Clock), .ClearPin(ClearPin),
    .Probe(genericreg_16_probe), .RegOut(genericreg_16_regout));
  // Probe on genericreg_17_probe
  GenericReg genericreg_17 (
    .WriteData(WriteData), .WriteEnable(decoder_1_out16[0]), .CLK(Clock), .ClearPin(ClearPin),
    .Probe(genericreg_17_probe), .RegOut(genericreg_17_regout));
  // Probe on genericreg_18_probe
  GenericReg genericreg_18 (
    .WriteData(WriteData), .WriteEnable(decoder_1_out16[1]), .CLK(Clock), .ClearPin(ClearPin),
    .Probe(genericreg_18_probe), .RegOut(genericreg_18_regout));
  // Probe on genericreg_19_probe
  GenericReg genericreg_19 (
    .WriteData(WriteData), .WriteEnable(decoder_1_out16[2]), .CLK(Clock), .ClearPin(ClearPin),
    .Probe(genericreg_19_probe), .RegOut(genericreg_19_regout));
  // Probe on genericreg_20_probe
  GenericReg genericreg_20 (
    .WriteData(WriteData), .WriteEnable(decoder_1_out16[3]), .CLK(Clock), .ClearPin(ClearPin),
    .Probe(genericreg_20_probe), .RegOut(genericreg_20_regout));
  // Probe on genericreg_21_probe
  GenericReg genericreg_21 (
    .WriteData(WriteData), .WriteEnable(decoder_1_out16[4]), .CLK(Clock), .ClearPin(ClearPin),
    .Probe(genericreg_21_probe), .RegOut(genericreg_21_regout));
  // Probe on genericreg_22_probe
  GenericReg genericreg_22 (
    .WriteData(WriteData), .WriteEnable(decoder_1_out16[5]), .CLK(Clock), .ClearPin(ClearPin),
    .Probe(genericreg_22_probe), .RegOut(genericreg_22_regout));
  // Probe on genericreg_23_probe
  GenericReg genericreg_23 (
    .WriteData(WriteData), .WriteEnable(decoder_1_out16[6]), .CLK(Clock), .ClearPin(ClearPin),
    .Probe(genericreg_23_probe), .RegOut(genericreg_23_regout));
  // Probe on genericreg_24_probe
  GenericReg genericreg_24 (
    .WriteData(WriteData), .WriteEnable(decoder_1_out16[7]), .CLK(Clock), .ClearPin(ClearPin),
    .Probe(genericreg_24_probe), .RegOut(genericreg_24_regout));
  Multiplexer #(.select(5), .width(32)) multiplexer_2 (
    .in0(genericreg_1_regout), .in1(genericreg_2_regout), .in2(genericreg_3_regout),
    .in3(genericreg_4_regout), .in4(genericreg_5_regout), .in5(genericreg_6_regout),
    .in6(genericreg_7_regout), .in7(genericreg_8_regout), .in8(genericreg_9_regout),
    .in9(genericreg_10_regout), .in10(genericreg_11_regout), .in11(genericreg_12_regout),
    .in12(genericreg_13_regout), .in13(genericreg_14_regout), .in14(genericreg_15_regout),
    .in15(genericreg_16_regout), .in16(genericreg_17_regout), .in17(genericreg_18_regout),
    .in18(genericreg_19_regout), .in19(genericreg_20_regout), .in20(genericreg_21_regout),
    .in21(genericreg_22_regout), .in22(genericreg_23_regout), .in23(genericreg_24_regout),
    .in24(genericreg_31_regout), .in25(genericreg_32_regout), .in26(genericreg_29_regout),
    .in27(genericreg_30_regout), .in28(genericreg_27_regout), .in29(genericreg_28_regout),
    .in30(genericreg_25_regout), .in31(genericreg_26_regout), .out(Register2), .sel(ReadRegister2));
  // Probe on genericreg_25_probe
  // Probe on genericreg_26_probe
  // Probe on genericreg_27_probe
  // Probe on genericreg_28_probe
  // Probe on genericreg_29_probe
  // Probe on genericreg_30_probe
  // Probe on genericreg_31_probe
  // Probe on genericreg_32_probe
  GenericReg genericreg_25 (
    .WriteData(WriteData), .WriteEnable(decoder_1_out24[0]), .CLK(Clock), .ClearPin(ClearPin),
    .Probe(genericreg_25_probe), .RegOut(genericreg_25_regout));
  GenericReg genericreg_26 (
    .WriteData(WriteData), .WriteEnable(decoder_1_out24[1]), .CLK(Clock), .ClearPin(ClearPin),
    .Probe(genericreg_26_probe), .RegOut(genericreg_26_regout));
  GenericReg genericreg_27 (
    .WriteData(WriteData), .WriteEnable(decoder_1_out24[2]), .CLK(Clock), .ClearPin(ClearPin),
    .Probe(genericreg_27_probe), .RegOut(genericreg_27_regout));
  GenericReg genericreg_28 (
    .WriteData(WriteData), .WriteEnable(decoder_1_out24[3]), .CLK(Clock), .ClearPin(ClearPin),
    .Probe(genericreg_28_probe), .RegOut(genericreg_28_regout));
  GenericReg genericreg_29 (
    .WriteData(WriteData), .WriteEnable(decoder_1_out24[4]), .CLK(Clock), .ClearPin(ClearPin),
    .Probe(genericreg_29_probe), .RegOut(genericreg_29_regout));
  GenericReg genericreg_30 (
    .WriteData(WriteData), .WriteEnable(decoder_1_out24[5]), .CLK(Clock), .ClearPin(ClearPin),
    .Probe(genericreg_30_probe), .RegOut(genericreg_30_regout));
  GenericReg genericreg_31 (
    .WriteData(WriteData), .WriteEnable(decoder_1_out24[6]), .CLK(Clock), .ClearPin(ClearPin),
    .Probe(genericreg_31_probe), .RegOut(genericreg_31_regout));
  GenericReg genericreg_32 (
    .WriteData(WriteData), .WriteEnable(decoder_1_out24[7]), .CLK(Clock), .ClearPin(ClearPin),
    .Probe(genericreg_32_probe), .RegOut(genericreg_32_regout));

  // Notes on the sheet:
  //   zero
  //   at
  //   v0
  //   v1
  //   a0
  //   a1
  //   a2
  //   a3
  //   t0
  //   t1
  //   t2
  //   t3
  //   t4
  //   t5
  //   t6
  //   t7
  //   s0
  //   s1
  //   s2
  //   s3
  //   s4
  //   s5
  //   s6
  //   s7
  //   t8
  //   t9
  //   k0
  //   k1
  //   gp
  //   sp
  //   fp
  //   ra
endmodule

module ALU0_30Bit (
  input  AInv,
  input  BInv,
  input  CIn,
  input  [1:0] ALUOp,
  input  A,
  input  B,
  input  Less,
  output Result,
  output COut
);

  wire and_1_out, and_2_out, and_3_out, multiplexer_1_out, multiplexer_2_out, not_1_out, not_2_out, or_1_out,
       xor_1_out, xor_2_out;

  not not_1 (not_1_out, A);
  not not_2 (not_2_out, B);
  Multiplexer multiplexer_1 (.in0(A), .in1(not_1_out), .out(multiplexer_1_out), .sel(AInv));
  Multiplexer multiplexer_2 (.in0(B), .in1(not_2_out), .out(multiplexer_2_out), .sel(BInv));
  and and_1 (and_1_out, multiplexer_1_out, multiplexer_2_out);
  or or_1 (or_1_out, multiplexer_1_out, multiplexer_2_out);
  and and_2 (and_2_out, multiplexer_1_out, multiplexer_2_out);
  xor xor_1 (xor_1_out, multiplexer_1_out, multiplexer_2_out);
  or or_2 (COut, and_2_out, and_3_out);
  and and_3 (and_3_out, xor_1_out, CIn);
  xor xor_2 (xor_2_out, CIn, xor_1_out);
  Multiplexer #(.select(2)) multiplexer_3 (
    .in0(and_1_out), .in1(or_1_out), .in2(xor_2_out), .in3(Less), .out(Result), .sel(ALUOp));
endmodule

module ALU31Bit (
  input  AInv,
  input  BInv,
  input  CIn,
  input  [1:0] ALUOp,
  input  A,
  input  B,
  input  Less,
  output Result,
  output Set,
  output Overflow,
  output COut
);

  wire and_1_out, and_2_out, and_3_out, multiplexer_1_out, multiplexer_2_out, not_1_out, not_2_out, or_1_out,
       xor_1_out;

  not not_1 (not_1_out, A);
  not not_2 (not_2_out, B);
  Multiplexer multiplexer_1 (.in0(A), .in1(not_1_out), .out(multiplexer_1_out), .sel(AInv));
  Multiplexer multiplexer_2 (.in0(B), .in1(not_2_out), .out(multiplexer_2_out), .sel(BInv));
  and and_1 (and_1_out, multiplexer_1_out, multiplexer_2_out);
  or or_1 (or_1_out, multiplexer_1_out, multiplexer_2_out);
  and and_2 (and_2_out, multiplexer_1_out, multiplexer_2_out);
  xor xor_1 (xor_1_out, multiplexer_1_out, multiplexer_2_out);
  or or_2 (COut, and_2_out, and_3_out);
  and and_3 (and_3_out, xor_1_out, CIn);
  xor xor_2 (Set, CIn, xor_1_out);
  Multiplexer #(.select(2)) multiplexer_3 (
    .in0(and_1_out), .in1(or_1_out), .in2(Set), .in3(Less), .out(Result), .sel(ALUOp));
  xor xor_3 (Overflow, CIn, COut);
endmodule

module ALU32Bits (
  input  [1:0] ALUOp,
  input  AInv,
  input  BInv,
  input  [31:0] OperandA,
  input  [31:0] OperandB,
  output [31:0] ALUResult,
  output Overflow,
  output ZeroComp
);

  wire alu0_30bit_1_cout, alu0_30bit_2_cout, alu0_30bit_3_cout, alu0_30bit_4_cout, alu0_30bit_5_cout,
       alu0_30bit_6_cout, alu0_30bit_7_cout, alu0_30bit_9_cout, alu0_30bit_10_cout, alu0_30bit_11_cout,
       alu0_30bit_12_cout, alu0_30bit_13_cout, alu0_30bit_14_cout, alu0_30bit_15_cout, alu0_30bit_17_cout,
       alu0_30bit_18_cout, alu0_30bit_19_cout, alu0_30bit_20_cout, alu0_30bit_21_cout, alu0_30bit_22_cout,
       alu0_30bit_23_cout, alu0_30bit_25_cout, alu0_30bit_26_cout, alu0_30bit_27_cout, alu0_30bit_28_cout,
       alu0_30bit_29_cout, alu0_30bit_30_cout, alu0_30bit_31_cout, COut7, COut15, COut23, SetOut;

  nor nor_1 (ZeroComp, ALUResult[0], ALUResult[1], ALUResult[2], ALUResult[3], ALUResult[4], ALUResult[5], ALUResult[6], ALUResult[7], ALUResult[8], ALUResult[9], ALUResult[10], ALUResult[11], ALUResult[12], ALUResult[13], ALUResult[14], ALUResult[15], ALUResult[16], ALUResult[17], ALUResult[18], ALUResult[19], ALUResult[20], ALUResult[21], ALUResult[22], ALUResult[23], ALUResult[24], ALUResult[25], ALUResult[26], ALUResult[27], ALUResult[28], ALUResult[29], ALUResult[30], ALUResult[31]);
  ALU0_30Bit alu0_30bit_1 (
    .AInv(AInv), .BInv(BInv), .CIn(BInv), .A(OperandA[0]), .B(OperandB[0]), .Less(SetOut), .ALUOp(ALUOp),
    .COut(alu0_30bit_1_cout), .Result(ALUResult[0]));
  ALU0_30Bit alu0_30bit_2 (
    .AInv(AInv), .BInv(BInv), .CIn(alu0_30bit_1_cout), .A(OperandA[1]), .B(OperandB[1]), .Less(1'b0),
    .ALUOp(ALUOp), .COut(alu0_30bit_2_cout), .Result(ALUResult[1]));
  ALU0_30Bit alu0_30bit_3 (
    .AInv(AInv), .BInv(BInv), .CIn(alu0_30bit_2_cout), .A(OperandA[2]), .B(OperandB[2]), .Less(1'b0),
    .ALUOp(ALUOp), .COut(alu0_30bit_3_cout), .Result(ALUResult[2]));
  ALU0_30Bit alu0_30bit_4 (
    .AInv(AInv), .BInv(BInv), .CIn(alu0_30bit_3_cout), .A(OperandA[3]), .B(OperandB[3]), .Less(1'b0),
    .ALUOp(ALUOp), .COut(alu0_30bit_4_cout), .Result(ALUResult[3]));
  ALU0_30Bit alu0_30bit_5 (
    .AInv(AInv), .BInv(BInv), .CIn(alu0_30bit_4_cout), .A(OperandA[4]), .B(OperandB[4]), .Less(1'b0),
    .ALUOp(ALUOp), .COut(alu0_30bit_5_cout), .Result(ALUResult[4]));
  ALU0_30Bit alu0_30bit_6 (
    .AInv(AInv), .BInv(BInv), .CIn(alu0_30bit_5_cout), .A(OperandA[5]), .B(OperandB[5]), .Less(1'b0),
    .ALUOp(ALUOp), .COut(alu0_30bit_6_cout), .Result(ALUResult[5]));
  ALU0_30Bit alu0_30bit_7 (
    .AInv(AInv), .BInv(BInv), .CIn(alu0_30bit_6_cout), .A(OperandA[6]), .B(OperandB[6]), .Less(1'b0),
    .ALUOp(ALUOp), .COut(alu0_30bit_7_cout), .Result(ALUResult[6]));
  ALU0_30Bit alu0_30bit_8 (
    .AInv(AInv), .BInv(BInv), .CIn(alu0_30bit_7_cout), .A(OperandA[7]), .B(OperandB[7]), .Less(1'b0),
    .ALUOp(ALUOp), .COut(COut7), .Result(ALUResult[7]));
  ALU0_30Bit alu0_30bit_9 (
    .AInv(AInv), .BInv(BInv), .CIn(COut7), .A(OperandA[8]), .B(OperandB[8]), .Less(1'b0), .ALUOp(ALUOp),
    .COut(alu0_30bit_9_cout), .Result(ALUResult[8]));
  ALU0_30Bit alu0_30bit_10 (
    .AInv(AInv), .BInv(BInv), .CIn(alu0_30bit_9_cout), .A(OperandA[9]), .B(OperandB[9]), .Less(1'b0),
    .ALUOp(ALUOp), .COut(alu0_30bit_10_cout), .Result(ALUResult[9]));
  ALU0_30Bit alu0_30bit_11 (
    .AInv(AInv), .BInv(BInv), .CIn(alu0_30bit_10_cout), .A(OperandA[10]), .B(OperandB[10]), .Less(1'b0),
    .ALUOp(ALUOp), .COut(alu0_30bit_11_cout), .Result(ALUResult[10]));
  ALU0_30Bit alu0_30bit_12 (
    .AInv(AInv), .BInv(BInv), .CIn(alu0_30bit_11_cout), .A(OperandA[11]), .B(OperandB[11]), .Less(1'b0),
    .ALUOp(ALUOp), .COut(alu0_30bit_12_cout), .Result(ALUResult[11]));
  ALU0_30Bit alu0_30bit_13 (
    .AInv(AInv), .BInv(BInv), .CIn(alu0_30bit_12_cout), .A(OperandA[12]), .B(OperandB[12]), .Less(1'b0),
    .ALUOp(ALUOp), .COut(alu0_30bit_13_cout), .Result(ALUResult[12]));
  ALU0_30Bit alu0_30bit_14 (
    .AInv(AInv), .BInv(BInv), .CIn(alu0_30bit_13_cout), .A(OperandA[13]), .B(OperandB[13]), .Less(1'b0),
    .ALUOp(ALUOp), .COut(alu0_30bit_14_cout), .Result(ALUResult[13]));
  ALU0_30Bit alu0_30bit_15 (
    .AInv(AInv), .BInv(BInv), .CIn(alu0_30bit_14_cout), .A(OperandA[14]), .B(OperandB[14]), .Less(1'b0),
    .ALUOp(ALUOp), .COut(alu0_30bit_15_cout), .Result(ALUResult[14]));
  ALU0_30Bit alu0_30bit_16 (
    .AInv(AInv), .BInv(BInv), .CIn(alu0_30bit_15_cout), .A(OperandA[15]), .B(OperandB[15]), .Less(1'b0),
    .ALUOp(ALUOp), .COut(COut15), .Result(ALUResult[15]));
  ALU0_30Bit alu0_30bit_17 (
    .AInv(AInv), .BInv(BInv), .CIn(COut15), .A(OperandA[16]), .B(OperandB[16]), .Less(1'b0), .ALUOp(ALUOp),
    .COut(alu0_30bit_17_cout), .Result(ALUResult[16]));
  ALU0_30Bit alu0_30bit_18 (
    .AInv(AInv), .BInv(BInv), .CIn(alu0_30bit_17_cout), .A(OperandA[17]), .B(OperandB[17]), .Less(1'b0),
    .ALUOp(ALUOp), .COut(alu0_30bit_18_cout), .Result(ALUResult[17]));
  ALU0_30Bit alu0_30bit_19 (
    .AInv(AInv), .BInv(BInv), .CIn(alu0_30bit_18_cout), .A(OperandA[18]), .B(OperandB[18]), .Less(1'b0),
    .ALUOp(ALUOp), .COut(alu0_30bit_19_cout), .Result(ALUResult[18]));
  ALU0_30Bit alu0_30bit_20 (
    .AInv(AInv), .BInv(BInv), .CIn(alu0_30bit_19_cout), .A(OperandA[19]), .B(OperandB[19]), .Less(1'b0),
    .ALUOp(ALUOp), .COut(alu0_30bit_20_cout), .Result(ALUResult[19]));
  ALU0_30Bit alu0_30bit_21 (
    .AInv(AInv), .BInv(BInv), .CIn(alu0_30bit_20_cout), .A(OperandA[20]), .B(OperandB[20]), .Less(1'b0),
    .ALUOp(ALUOp), .COut(alu0_30bit_21_cout), .Result(ALUResult[20]));
  ALU0_30Bit alu0_30bit_22 (
    .AInv(AInv), .BInv(BInv), .CIn(alu0_30bit_21_cout), .A(OperandA[21]), .B(OperandB[21]), .Less(1'b0),
    .ALUOp(ALUOp), .COut(alu0_30bit_22_cout), .Result(ALUResult[21]));
  ALU0_30Bit alu0_30bit_23 (
    .AInv(AInv), .BInv(BInv), .CIn(alu0_30bit_22_cout), .A(OperandA[22]), .B(OperandB[22]), .Less(1'b0),
    .ALUOp(ALUOp), .COut(alu0_30bit_23_cout), .Result(ALUResult[22]));
  ALU0_30Bit alu0_30bit_24 (
    .AInv(AInv), .BInv(BInv), .CIn(alu0_30bit_23_cout), .A(OperandA[23]), .B(OperandB[23]), .Less(1'b0),
    .ALUOp(ALUOp), .COut(COut23), .Result(ALUResult[23]));
  ALU0_30Bit alu0_30bit_25 (
    .AInv(AInv), .BInv(BInv), .CIn(COut23), .A(OperandA[24]), .B(OperandB[24]), .Less(1'b0), .ALUOp(ALUOp),
    .COut(alu0_30bit_25_cout), .Result(ALUResult[24]));
  ALU0_30Bit alu0_30bit_26 (
    .AInv(AInv), .BInv(BInv), .CIn(alu0_30bit_25_cout), .A(OperandA[25]), .B(OperandB[25]), .Less(1'b0),
    .ALUOp(ALUOp), .COut(alu0_30bit_26_cout), .Result(ALUResult[25]));
  ALU0_30Bit alu0_30bit_27 (
    .AInv(AInv), .BInv(BInv), .CIn(alu0_30bit_26_cout), .A(OperandA[26]), .B(OperandB[26]), .Less(1'b0),
    .ALUOp(ALUOp), .COut(alu0_30bit_27_cout), .Result(ALUResult[26]));
  ALU0_30Bit alu0_30bit_28 (
    .AInv(AInv), .BInv(BInv), .CIn(alu0_30bit_27_cout), .A(OperandA[27]), .B(OperandB[27]), .Less(1'b0),
    .ALUOp(ALUOp), .COut(alu0_30bit_28_cout), .Result(ALUResult[27]));
  ALU0_30Bit alu0_30bit_29 (
    .AInv(AInv), .BInv(BInv), .CIn(alu0_30bit_28_cout), .A(OperandA[28]), .B(OperandB[28]), .Less(1'b0),
    .ALUOp(ALUOp), .COut(alu0_30bit_29_cout), .Result(ALUResult[28]));
  ALU0_30Bit alu0_30bit_30 (
    .AInv(AInv), .BInv(BInv), .CIn(alu0_30bit_29_cout), .A(OperandA[29]), .B(OperandB[29]), .Less(1'b0),
    .ALUOp(ALUOp), .COut(alu0_30bit_30_cout), .Result(ALUResult[29]));
  ALU0_30Bit alu0_30bit_31 (
    .AInv(AInv), .BInv(BInv), .CIn(alu0_30bit_30_cout), .A(OperandA[30]), .B(OperandB[30]), .Less(1'b0),
    .ALUOp(ALUOp), .COut(alu0_30bit_31_cout), .Result(ALUResult[30]));
  ALU31Bit alu31bit_1 (
    .AInv(AInv), .BInv(BInv), .CIn(alu0_30bit_31_cout), .A(OperandA[31]), .B(OperandB[31]), .Less(1'b0),
    .ALUOp(ALUOp), .Set(SetOut), .Result(ALUResult[31]), .Overflow(Overflow));  // open: COut

  // Other names for the same wires on the sheet: ALUOut[31:0] = ALUResult; Ab0_7[7:0] = OperandA[7:0];
  //   Ab8_15[7:0] = OperandA[15:8]; Ab16_23[7:0] = OperandA[23:16]; Ab24_31[7:0] = OperandA[31:24];
  //   Bb0_7[7:0] = OperandB[7:0]; Bb8_15[7:0] = OperandB[15:8]; Bb16_23[7:0] = OperandB[23:16];
  //   Bb24_31[7:0] = OperandB[31:24]
endmodule

module ALUControl (
  input  [5:0] Funct,
  input  [1:0] ALUOp,
  output AInv,
  output BInv,
  output [1:0] ALUOperationSel
);

  wire and_2_out, and_3_out, and_4_out, and_5_out, and_6_out, and_7_out, and_8_out, and_9_out, and_10_out,
       and_11_out, not_1_out, not_2_out, not_3_out, not_4_out;

  not not_1 (not_1_out, Funct[2]);
  not not_2 (not_2_out, Funct[1]);
  not not_3 (not_3_out, Funct[0]);
  not not_4 (not_4_out, ALUOp[1]);
  and and_1 (AInv, Funct[2], Funct[1], ALUOp[1]);
  and and_2 (and_2_out, not_4_out, ALUOp[0]);
  and and_3 (and_3_out, Funct[0], ALUOp[0]);
  and and_4 (and_4_out, Funct[1], ALUOp[1]);
  and and_5 (and_5_out, Funct[2], ALUOp[0]);
  and and_6 (and_6_out, Funct[3], ALUOp[0]);
  and and_7 (and_7_out, Funct[4], ALUOp[0]);
  and and_8 (and_8_out, Funct[5], ALUOp[0]);
  or or_1 (ALUOperationSel[1], not_1_out, not_4_out);
  and and_9 (and_9_out, not_2_out, Funct[0], ALUOp[1]);
  and and_10 (and_10_out, Funct[2], Funct[1], not_3_out, ALUOp[1]);
  and and_11 (and_11_out, Funct[3], ALUOp[1]);
  or or_2 (ALUOperationSel[0], and_9_out, and_10_out, and_11_out);
  or or_3 (BInv, and_2_out, and_3_out, and_4_out, and_5_out, and_6_out, and_7_out, and_8_out);
endmodule

module JumpCircuit (
  input  [31:0] PC,
  input  [25:0] JumpAddr,
  output [31:0] JumpAddress32
);

  wire [27:0] bit_extender_1_out;

  assign bit_extender_1_out = {{2{1'b0}}, JumpAddr};  // Bit_Extender bit_extender_1
  Shifter #(.width(28)) shifter_1 (.in(bit_extender_1_out), .\dist (5'b00010), .out(JumpAddress32[27:0]));

  assign JumpAddress32[31:28] = PC[31:28];
endmodule

module GenericReg (
  input  [31:0] WriteData,
  input  WriteEnable,
  input  CLK,
  input  ClearPin,
  output [31:0] Probe,
  output [31:0] RegOut
);

  Register #(.width(32)) register_1 (.D(WriteData), .en(WriteEnable), .clk(CLK), .Q(Probe), .clr(ClearPin));

  assign RegOut = Probe;
endmodule

module NewPCCircuit (
  input  Branch,
  input  Jump,
  input  ALUZero,
  input  [31:0] PC,
  input  [31:0] SExtImmd,
  input  [25:0] JAddr,
  output [31:0] out_7
);

  wire and_1_out;
  wire [31:0] adder_1_out, adder_2_out, jumpcircuit_1_jumpaddress32, multiplexer_1_out, shifter_1_out;

  Adder #(.width(32)) adder_1 (.a(32'h4), .b(PC), .out(adder_1_out));  // open: cin, cout
  Shifter #(.width(32)) shifter_1 (.in(SExtImmd), .\dist (5'b00010), .out(shifter_1_out));
  Adder #(.width(32)) adder_2 (.a(adder_1_out), .b(shifter_1_out), .out(adder_2_out));  // open: cin, cout
  JumpCircuit jumpcircuit_1 (.PC(PC), .JumpAddr(JAddr), .JumpAddress32(jumpcircuit_1_jumpaddress32));
  and and_1 (and_1_out, Branch, ALUZero);
  Multiplexer #(.width(32)) multiplexer_1 (
    .in0(adder_1_out), .in1(adder_2_out), .out(multiplexer_1_out), .sel(and_1_out));
  Multiplexer #(.width(32)) multiplexer_2 (
    .in0(multiplexer_1_out), .in1(jumpcircuit_1_jumpaddress32), .out(out_7), .sel(Jump));

  // Other names for the same wires on the sheet: JumpA[25:0] = JAddr
endmodule
